# Fritzing sketch cerebrofono-v2 (saved by Fritzing 0.9.3b)

parts:
  Componente7 = Arduino Nano (Rev3.0)
  Componente8 = Audio FX Sound Board
  Power_plug1 = Power plug
  C2 = Electrolytic Capacitor [capacitance=100μF package="0807 [SMD, electrolytic]"]
  Part5 = Adafruit Breadboard-Friendly NeoPixel [part_number="Adafruit #1312"]
  R2 = Resistor [tolerance=±5% resistance=470 package=THT]
  Componente9 = RFID USB Reader

nets:
  GND: Componente7.GND, Componente8.GND, Power_plug1.GND, C2.-, Part5.GND, Componente9.GND
  N1: Componente7.D2, Componente9.TX-O
  N2: Componente7.D4, R2.Pin_0
  N3: Componente7.D6, Componente8.RST
  N4: Componente7.D7, Componente8.ACT
  N5: Componente7.D8, Componente8.0
  N6: Componente7.D9, Componente8.1
  N7: Componente7.D10, Componente8.2
  N8: Componente7.D11/MOSI, Componente8.3
  N9: Componente7.D12/MISO, Componente8.4
  5V: Componente7.5V, Componente8.VIN, Componente9.VCC
  VCC: Power_plug1.VCC, C2.+, Part5.VDD
  N10: Part5.IN, R2.Pin_1

notes:
  470 Ohm
  1000 uF
  5V Supply

custom parts:
  Audio FX Sound Board: The Adafruit Sound Board, the fastest way to add audio effects to a project!
  Adafruit Breadboard-Friendly NeoPixel: This is the easiest way possible to add small, bright RGB pixels to your project. We took the same technology from our Flora NeoPixels and made them breadboard friendly, with two rows of 3 x 0.1" spaced header on each side for easy soldering, chaining and breadboarding. These ultra-bright LEDs have a constant-current driver cooked right into the LED package! The pixels are chainable - so you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
