# Fritzing sketch candles (saved by Fritzing 0.9.3b)
breadboards: 1

parts:
  Nano = Arduino Nano (Rev3.0)
  Relay_1 = IC, SIP package, 3 pins
  Relay_2 = IC, SIP package, 3 pins
  Relay_3 = IC, SIP package, 3 pins
  Relay_4 = IC, SIP package, 3 pins
  Mic_1 = Breakout Board for Electret Microphone
  Mic_2 = Breakout Board for Electret Microphone
  Mic_3 = Breakout Board for Electret Microphone
  Mic_4 = Breakout Board for Electret Microphone

nets:
  GND: Nano.GND, Relay_1.pin2, Relay_2.pin2, Relay_3.pin2, Relay_4.pin2, Mic_1.GND, Mic_2.GND, Mic_3.GND, Mic_4.GND
  D2: Nano.D2, Relay_1.pin3
  D3: Nano.D3, Relay_2.pin3
  D4: Nano.D4, Relay_3.pin3
  D5: Nano.D5, Relay_4.pin3
  5V: Nano.5V, Relay_1.pin1, Relay_2.pin1, Relay_3.pin1, Relay_4.pin1, Mic_1.VCC, Mic_2.VCC, Mic_3.VCC, Mic_4.VCC
  A3: Nano.A3, Mic_4.AUD
  A2: Nano.A2, Mic_3.AUD
  A1: Nano.A1, Mic_2.AUD
  A0: Nano.A0, Mic_1.AUD
