# Fritzing sketch maletin-fono (saved by Fritzing 0.9.3b)

parts:
  Feather_M4_+_Music_Wing_+_OLED_Wing = Adafruit Feather M0 Express
  KEYPAD1 = Membrane Matrix Keypad
  I2C_LCD = IC, SIP package, 4 pins [chip_label="I2C LCD"]

nets:
  A5: Feather_M4_+_Music_Wing_+_OLED_Wing.A5, KEYPAD1.7
  A4: Feather_M4_+_Music_Wing_+_OLED_Wing.A4, KEYPAD1.6
  A3: Feather_M4_+_Music_Wing_+_OLED_Wing.A3, KEYPAD1.5
  A2: Feather_M4_+_Music_Wing_+_OLED_Wing.A2, KEYPAD1.4
  GND: Feather_M4_+_Music_Wing_+_OLED_Wing.GND, I2C_LCD.pin1
  3V: Feather_M4_+_Music_Wing_+_OLED_Wing.+3V3, I2C_LCD.pin2
  SCL: Feather_M4_+_Music_Wing_+_OLED_Wing.SCL, I2C_LCD.pin4
  SDA: Feather_M4_+_Music_Wing_+_OLED_Wing.SDA, I2C_LCD.pin3
  D11: KEYPAD1.1
  D12: KEYPAD1.2
  D13: KEYPAD1.3

custom parts:
  Adafruit Feather M0 Express: We love all our Feathers equally, but this Feather is very special. It's our first Feather that is specifically designed for use with CircuitPython! CircuitPython is our beginner-oriented flavor of MicroPython - and as the name hints at, its a small but full-featured version of the popular Python programming language specifically for use with circuitry and electronics. That doesn't mean you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
  Membrane Matrix Keypad: Membrane Matrix 3x4 Keypad
