# Fritzing sketch quiz (saved by Fritzing 0.9.3b)

parts:
  Part1 = Arduino Nano (Rev3.0)
  S1 = Round Pushbutton
  S2 = Round Pushbutton
  S3 = Round Pushbutton
  S4 = Round Pushbutton
  S5 = Round Pushbutton
  S6 = Round Pushbutton
  S7 = Round Pushbutton
  Part7 = Adafruit Breadboard-Friendly NeoPixel [part_number="Adafruit #1312"]
  Power_plug3 = Power plug
  C4 = Electrolytic Capacitor [capacitance=100μF package="0807 [SMD, electrolytic]"]
  Part8 = Adafruit Breadboard-Friendly NeoPixel [part_number="Adafruit #1312"]
  Part9 = Adafruit Breadboard-Friendly NeoPixel [part_number="Adafruit #1312"]
  Part10 = Adafruit Breadboard-Friendly NeoPixel [part_number="Adafruit #1312"]
  Part11 = Adafruit Breadboard-Friendly NeoPixel [part_number="Adafruit #1312"]
  R4 = Resistor [tolerance=±5% resistance=470 package=THT]
  R5 = Resistor [tolerance=±5% resistance=470 package=THT]
  R6 = Resistor [tolerance=±5% resistance=470 package=THT]
  R7 = Resistor [tolerance=±5% resistance=470 package=THT]
  R8 = Resistor [tolerance=±5% resistance=470 package=THT]
  LED1 = LED - 3mm [color="Red (633nm)" package="3 mm [THT]"]
  LED2 = LED - 3mm [color="Red (633nm)" package="3 mm [THT]"]
  LED3 = LED - 3mm [color="Red (633nm)" package="3 mm [THT]"]
  LED4 = LED - 3mm [color="Red (633nm)" package="3 mm [THT]"]
  LED5 = LED - 3mm [color="Red (633nm)" package="3 mm [THT]"]
  LED6 = LED - 3mm [color="Red (633nm)" package="3 mm [THT]"]

nets:
  GND: Part1.GND, S7.leg0, Part7.IN, Part7.GND, Power_plug3.GND, C4.-, Part8.IN, Part8.GND, Part9.GND, Part10.IN, Part10.GND, Part11.IN, Part11.GND, R4.Pin_0, R6.Pin_0, R7.Pin_0, R8.Pin_0
  N1: Part1.D2, S5.leg1
  N2: Part1.D3, S6.leg1
  N3: Part1.D4, S3.leg1
  N4: Part1.D5, S4.leg1
  N5: Part1.D6, S2.leg1
  N6: Part1.D7, S1.leg0, S1.leg1, S2.leg0, S3.leg0, S4.leg0, S5.leg0, S6.leg0
  N7: Part1.D8, R7.Pin_1
  N8: Part1.D9, R6.Pin_1
  N9: Part1.D10, R5.Pin_1
  N10: Part1.D11/MOSI, R4.Pin_1
  N11: Part1.D12/MISO, R8.Pin_1
  N12: Part1.A6, S7.leg1
  VDD: Part7.VDD, Power_plug3.VCC, C4.+, Part8.VDD, Part9.VDD, Part10.VDD, Part11.VDD
  N13: Part9.IN, R5.Pin_0
  N14: LED1.cathode, LED2.cathode, LED3.cathode, LED4.cathode, LED5.cathode, LED6.cathode

notes:
  5V Supply
  1000 uF

custom parts:
  Adafruit Breadboard-Friendly NeoPixel: This is the easiest way possible to add small, bright RGB pixels to your project. We took the same technology from our Flora NeoPixels and made them breadboard friendly, with two rows of 3 x 0.1" spaced header on each side for easy soldering, chaining and breadboarding. These ultra-bright LEDs have a constant-current driver cooked right into the LED package! The pixels are chainable - so you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
