# Fritzing sketch runebook (saved by Fritzing 0.9.3b)

parts:
  Part1 = Arduino Mega 2560 (Rev3)
  Q7 = PNP-Transistor [package="TO92 [THT]"]
  Q8 = PNP-Transistor [package="TO92 [THT]"]
  Q13 = PNP-Transistor [package="TO92 [THT]"]
  Q14 = PNP-Transistor [package="TO92 [THT]"]
  Q15 = PNP-Transistor [package="TO92 [THT]"]
  Q16 = PNP-Transistor [package="TO92 [THT]"]
  Q17 = PNP-Transistor [package="TO92 [THT]"]
  Q18 = PNP-Transistor [package="TO92 [THT]"]
  Part6 = Adafruit Breadboard-Friendly NeoPixel [part_number="Adafruit #1312"]
  Power_plug2 = Power plug
  C3 = Electrolytic Capacitor [capacitance=100μF package="0807 [SMD, electrolytic]"]
  R3 = Resistor [tolerance=±5% resistance=470 package=THT]
  Part7 = Adafruit Breadboard-Friendly NeoPixel [part_number="Adafruit #1312"]
  R4 = Resistor [tolerance=±5% resistance=470 package=THT]
  Q9 = PNP-Transistor [package="TO92 [THT]"]
  J1 = Basic Servo

nets:
  N1: Part1.D20/SDA, Part6.OUT, R3.Pin_0
  GND: Part1.GND, Q7.E, Q8.E, Q13.E, Q14.E, Q15.E, Q16.E, Q17.E, Q18.E, Part6.GND, Power_plug2.GND, C3.-, Part7.GND, Q9.E
  N2: Part1.D12_PWM, J1.pulse
  N3: Part1.D11_PWM, Q17.C
  N4: Part1.D10_PWM, Q18.C
  N5: Part1.D9_PWM, Q16.C
  N6: Part1.D8_PWM, Q14.C
  N7: Part1.5V, Q7.B, Q8.B, Q13.B, Q14.B, Q15.B, Q16.B, Q17.B, Q18.B, Q9.B
  N8: Part1.D3_PWM, Q9.C
  N9: Part1.D4_PWM, Q7.C
  N10: Part1.D5_PWM, Q8.C
  N11: Part1.D6_PWM, Q13.C
  N12: Part1.D7_PWM, Q15.C
  N13: Part1.D22, R4.Pin_0
  N14: Part6.IN, R3.Pin_1
  VDD: Part6.VDD, Power_plug2.VCC, C3.+, Part7.VDD
  N15: Part7.IN, R4.Pin_1

notes:
  00
  < 12V
  03
  06
  21
  24
  42
  27
  45
  48
  5V Supply
  12V
  Book
  Pipes
  NPN NO Inductive Sensors

custom parts:
  Adafruit Breadboard-Friendly NeoPixel: This is the easiest way possible to add small, bright RGB pixels to your project. We took the same technology from our Flora NeoPixels and made them breadboard friendly, with two rows of 3 x 0.1" spaced header on each side for easy soldering, chaining and breadboarding. These ultra-bright LEDs have a constant-current driver cooked right into the LED package! The pixels are chainable - so you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
